// Logisim project cpu.circ as structural Verilog: 16 circuits, main circuit main
module main (
  output [7:0] OutPut
);

  wire and_1_out, and_2_out, and_3_out, and_4_out, and_5_out, and_6_out, and_7_out, and_8_out, branch_taken,
       cfregister_1_c_q, Clock, ClockEnable, EX_MEM_HT, EX_MEM_MR, EX_MEM_MW, EX_MEM_OE, EX_MEM_RW,
       ID_EX_BNZ, ID_EX_BSrc, ID_EX_BZ, ID_EX_CW, ID_EX_HT, ID_EX_JMP, ID_EX_MR, ID_EX_MW, ID_EX_OE,
       ID_EX_RW, IR_BNZ, IR_BSrc, IR_BZ, IR_CWrite, IR_Halt, IR_Jump, IR_MemRead, IR_MemWrite, IR_OntEn,
       IR_RegWrite, MEM_WB_HT, MEM_WB_MR, MEM_WB_OE, MEM_WB_RW, n8bit_alu_1_cf, n8bit_alu_1_zf, not_2_out,
       nPause, or_1_out, or_2_out, Pause, Reset;
  wire [3:0] EX_MEM_rd, ID_EX_ALUop, ID_EX_rd, ID_EX_rsA, ID_EX_rsB, IR_ALUop, IR_rdC, IR_rsA, IR_rsB,
       MEM_WB_rd;
  wire [7:0] ALU_A, ALU_B, EX_MEM_ALUResult, EX_MEM_MemData, EX_MEM_WriteData, forwarding_unit_2_out_12,
       ID_EX_ALUResult, ID_EX_Imm, ID_EX_ReadA, ID_EX_ReadB, IR_Imm, MEM_WB_ALUResult, MEM_WB_MemData,
       MEM_WB_WriteBackData, multiplexer_1_out, pc_1_pc, registers_1_a, registers_1_b;
  wire [23:0] ir_1_ir_output, rom_1_data;

  Stop stop_1 (
    .ID_EX_rd(ID_EX_rd), .rA(IR_rsA), .rB(IR_rsB), .ID_EX_RegWrite(ID_EX_RW), .ID_EX_MemRead(ID_EX_MR),
    .stall(Pause), .nstall(nPause));
  // Probe on ID_EX_rsA
  or or_1 (or_1_out, ID_EX_JMP, branch_taken);
  and and_1 (and_1_out, nPause, ClockEnable);
  or or_2 (or_2_out, Pause, or_1_out);
  PC pc_1 (.Data(ID_EX_Imm), .Jump(or_1_out), .PC(pc_1_pc), .Clock(Clock), .Reset(Reset), .Enable(and_1_out));
  forwarding_unit forwarding_unit_1 (
    .ID_EX_ReadData(ID_EX_ReadA), .out_12(ALU_A), .EX_MEM_ALUResult(EX_MEM_ALUResult),
    .MEM_WB_ALUResult(MEM_WB_ALUResult), .MEM_WB_MemData(MEM_WB_MemData), .MEM_WB_MemRead(MEM_WB_MR),
    .Src(ID_EX_rsA), .EX_MEM_rd(EX_MEM_rd), .Ex_MEM_RegWrite(EX_MEM_RW), .EX_MEM_MemRead(EX_MEM_MR),
    .MEM_WB_rd(MEM_WB_rd), .MEM_WB_RegWrite(MEM_WB_RW));
  // Probe on pc_1_pc
  // Probe on ALU_A
  EX_MEM ex_mem_1 (
    .ALUResult(ID_EX_ALUResult), .WriteData(multiplexer_1_out), .rd(ID_EX_rd), .RegWrite(ID_EX_RW),
    .MemWrite(ID_EX_MW), .MemRead(ID_EX_MR), .OutEn(ID_EX_OE), .Halt(ID_EX_HT),
    .ALUResult_2(EX_MEM_ALUResult), .WriteData_2(EX_MEM_WriteData), .rd_2(EX_MEM_rd), .RegWrite_2(EX_MEM_RW),
    .MemWrite_2(EX_MEM_MW), .MemRead_2(EX_MEM_MR), .OutEn_2(EX_MEM_OE), .Halt_2(EX_MEM_HT), .Clock(Clock),
    .Reset(Reset), .Enable(ClockEnable));
  MEM_WB mem_wb_1 (
    .ALUResult(EX_MEM_ALUResult), .MemData(EX_MEM_MemData), .rd(EX_MEM_rd), .RegWrite(EX_MEM_RW),
    .MemRead(EX_MEM_MR), .OutEn(EX_MEM_OE), .Halt(EX_MEM_HT), .Enable(ClockEnable),
    .ALUResult_2(MEM_WB_ALUResult), .MemData_2(MEM_WB_MemData), .rd_2(MEM_WB_rd), .RegWrite_2(MEM_WB_RW),
    .MemRead_2(MEM_WB_MR), .OutEn_2(MEM_WB_OE), .Halt_2(MEM_WB_HT), .Clock(Clock), .Reset(Reset));
  // Probe on EX_MEM_rd
  // Probe on MEM_WB_rd
  ROM #(.dataWidth(24)) rom_1 (.addr(pc_1_pc), .data(rom_1_data));  // open: sel
  IR ir_1 (
    .IR_input(rom_1_data), .Enable(and_1_out), .IR_output(ir_1_ir_output), .Flush(or_1_out), .Clock(Clock),
    .Reset(Reset));
  Decoder decoder_1 (
    .IR(ir_1_ir_output), .rs2(IR_rsB), .rs1(IR_rsA), .ALUop(IR_ALUop), .CWrite(IR_CWrite),
    .RegWrite(IR_RegWrite), .MemRead(IR_MemRead), .MemWrite(IR_MemWrite), .BSrc(IR_BSrc), .BranchZ(IR_BZ),
    .BranchNZ(IR_BNZ), .Jump(IR_Jump), .OutEn(IR_OntEn), .Halt(IR_Halt), .Imm(IR_Imm), .rd(IR_rdC));
  ID_EX id_ex_1 (
    .Imm(IR_Imm), .ReadA(registers_1_a), .ReadB(registers_1_b), .ALUop(IR_ALUop), .Enable(ClockEnable),
    .rsA(IR_rsA), .Clock(Clock), .rsB(IR_rsB), .Reset(Reset), .rdC(IR_rdC), .RegWrite(IR_RegWrite),
    .MemWrite(IR_MemWrite), .MemRead(IR_MemRead), .BSrc(IR_BSrc), .BZ(IR_BZ), .BNZ(IR_BNZ), .JMP(IR_Jump),
    .CWrite(IR_CWrite), .OutEn(IR_OntEn), .Halt(IR_Halt), .Imm_2(ID_EX_Imm), .ReadA_2(ID_EX_ReadA),
    .ReadB_2(ID_EX_ReadB), .ALUop_2(ID_EX_ALUop), .rsA_2(ID_EX_rsA), .rsB_2(ID_EX_rsB), .rdC_2(ID_EX_rd),
    .RegWrite_2(ID_EX_RW), .MemWrite_2(ID_EX_MW), .MemRead_2(ID_EX_MR), .BSrc_2(ID_EX_BSrc), .BZ_2(ID_EX_BZ),
    .BNZ_2(ID_EX_BNZ), .JMP_2(ID_EX_JMP), .CWrite_2(ID_EX_CW), .OutEn_2(ID_EX_OE), .Halt_2(ID_EX_HT),
    .flush(or_2_out));
  // Probe on ID_EX_rsB
  and and_2 (and_2_out, ID_EX_MW, ID_EX_BSrc);
  Multiplexer #(.width(8), .enable("false")) multiplexer_1 (
    .in0(ALU_B), .in1(ALU_A), .out(multiplexer_1_out), .sel(and_2_out));
  // Probe on EX_MEM_WriteData
  // Probe on ID_EX_rd
  forwarding_unit forwarding_unit_2 (
    .ID_EX_ReadData(ID_EX_ReadB), .out_12(forwarding_unit_2_out_12), .EX_MEM_ALUResult(EX_MEM_ALUResult),
    .MEM_WB_ALUResult(MEM_WB_ALUResult), .MEM_WB_MemData(MEM_WB_MemData), .MEM_WB_MemRead(MEM_WB_MR),
    .Src(ID_EX_rsB), .EX_MEM_rd(EX_MEM_rd), .Ex_MEM_RegWrite(EX_MEM_RW), .EX_MEM_MemRead(EX_MEM_MR),
    .MEM_WB_rd(MEM_WB_rd), .MEM_WB_RegWrite(MEM_WB_RW));
  and and_3 (and_3_out, MEM_WB_OE, ClockEnable);
  Multiplexer #(.width(8), .enable("false")) multiplexer_2 (
    .in0(forwarding_unit_2_out_12), .in1(ID_EX_Imm), .out(ALU_B), .sel(ID_EX_BSrc));
  // Probe on ALU_B
  not not_1 (ClockEnable, MEM_WB_HT);
  OutPutRegister outputregister_1 (
    .Input(MEM_WB_ALUResult), .Enable(and_3_out), .Output(OutPut), .Clock(Clock), .Reset(Reset));
  Clock clock_1 (.out(Clock));
  Button u_Reset (.out(Reset));
  // Probe on EX_MEM_ALUResult
  and and_4 (and_4_out, EX_MEM_MW, ClockEnable);
  Multiplexer #(.width(8), .enable("false")) multiplexer_3 (
    .in0(MEM_WB_ALUResult), .in1(MEM_WB_MemData), .out(MEM_WB_WriteBackData), .sel(MEM_WB_MR));
  Registers registers_1 (
    .Data(MEM_WB_WriteBackData), .Address(MEM_WB_rd), .A_SEL(IR_rsA), .B_SEL(IR_rsB), .Write(and_5_out),
    .Clock(Clock), .A(registers_1_a), .B(registers_1_b), .Reset(Reset));
  // Probe on ID_EX_ALUop
  // Probe on MEM_WB_WriteBackData
  // Probe on registers_1_a
  // Probe on registers_1_b
  and and_5 (and_5_out, ClockEnable, MEM_WB_RW);
  _8bit_ALU u_8bit_alu_1 (
    .A(ALU_A), .B(ALU_B), .CF(n8bit_alu_1_cf), .Result(ID_EX_ALUResult), .Cin(cfregister_1_c_q),
    .Op(ID_EX_ALUop), .ZF(n8bit_alu_1_zf));
  // Probe on EX_MEM_MemData
  RAM #(.bus("separate")) ram_1 (
    .addr(EX_MEM_ALUResult), .din(EX_MEM_WriteData), .data(EX_MEM_MemData), .str(and_4_out), .clk(Clock),
    .clr(Reset));  // open: sel, ld
  and and_6 (and_6_out, n8bit_alu_1_zf, ID_EX_BZ);
  not not_2 (not_2_out, n8bit_alu_1_zf);
  and and_7 (and_7_out, not_2_out, ID_EX_BNZ);
  and and_8 (and_8_out, ClockEnable, ID_EX_CW);
  CFRegister cfregister_1 (
    .CF(n8bit_alu_1_cf), .Enable(and_8_out), .C_Q(cfregister_1_c_q), .Clock(Clock), .Reset(Reset));
  // Probe on ID_EX_ALUResult
  or or_3 (branch_taken, and_6_out, and_7_out);

  // Notes on the sheet:
  //   contents of rom_1 (hex, n*v repeats v):
  //   281000 283000 2820ff 284001 105240 116130 a00500 a00600 b00000
endmodule

module CLA_Generator (
  input  P3,
  input  G3,
  input  P2,
  input  G2,
  input  P1,
  input  G1,
  input  P0,
  input  G0,
  input  C0,
  output Cout,
  output S3,
  output C3,
  output S2,
  output C2,
  output S1,
  output C1,
  output S0
);

  wire and_1_out, and_2_out, and_3_out, and_4_out, and_5_out, and_6_out, and_7_out, and_8_out, and_9_out,
       and_10_out, and_11_out, and_12_out, and_13_out, and_14_out, and_15_out, and_16_out, or_2_out,
       or_4_out, or_6_out;

  and and_1 (and_1_out, P3, G2);
  and and_2 (and_2_out, P3, P2, G1);
  and and_3 (and_3_out, P3, P2, P1, G0);
  and and_4 (and_4_out, P3, P2, P1, P0, C0);
  and and_5 (and_5_out, P2, G1);
  and and_6 (and_6_out, P2, P1, G0);
  and and_7 (and_7_out, P2, P1, P0, C0);
  and and_8 (and_8_out, P2, G1);
  and and_9 (and_9_out, P2, P1, G0);
  and and_10 (and_10_out, P2, P1, P0, C0);
  and and_11 (and_11_out, P1, G0);
  and and_12 (and_12_out, P1, P0, C0);
  and and_13 (and_13_out, P1, G0);
  and and_14 (and_14_out, P1, P0, C0);
  and and_15 (and_15_out, P0, C0);
  and and_16 (and_16_out, P0, C0);
  xor xor_1 (S0, P0, C0);
  or or_1 (Cout, G3, and_1_out, and_2_out, and_3_out, and_4_out);
  or or_2 (or_2_out, G2, and_5_out, and_6_out, and_7_out);
  or or_3 (C3, G2, and_8_out, and_9_out, and_10_out);
  or or_4 (or_4_out, G1, and_11_out, and_12_out);
  or or_5 (C2, G1, and_13_out, and_14_out);
  or or_6 (or_6_out, G0, and_15_out);
  or or_7 (C1, G0, and_16_out);
  xor xor_2 (S3, P3, or_2_out);
  xor xor_3 (S2, P2, or_4_out);
  xor xor_4 (S1, P1, or_6_out);
endmodule

module _4bit_CLA (
  input  B3,
  input  A3,
  input  B2,
  input  A2,
  input  B1,
  input  A1,
  input  B0,
  input  A0,
  input  Cin,
  output Cout,
  output S3,
  output C3,
  output S2,
  output S1,
  output S0
);

  wire and_1_out, and_2_out, and_3_out, and_4_out, xor_1_out, xor_2_out, xor_3_out, xor_4_out;

  and and_1 (and_1_out, B3, A3);
  and and_2 (and_2_out, B2, A2);
  and and_3 (and_3_out, B1, A1);
  and and_4 (and_4_out, B0, A0);
  xor xor_1 (xor_1_out, B3, A3);
  xor xor_2 (xor_2_out, B2, A2);
  xor xor_3 (xor_3_out, B1, A1);
  xor xor_4 (xor_4_out, B0, A0);
  CLA_Generator cla_generator_1 (
    .P3(xor_1_out), .G3(and_1_out), .P2(xor_2_out), .G2(and_2_out), .P1(xor_3_out), .G1(and_3_out),
    .P0(xor_4_out), .G0(and_4_out), .C0(Cin), .Cout(Cout), .S3(S3), .C3(C3), .S2(S2), .S1(S1), .S0(S0));  // open: C2, C1
endmodule

module _8bit_CLA (
  input  [7:0] B,
  input  [7:0] A,
  input  SUB,
  input  Cin,
  output CF,
  output OF,
  output SF,
  output ZF,
  output [7:0] Sum
);

  wire n4bit_cla_1_c3, n4bit_cla_1_cout, n4bit_cla_2_cout, xor_1_out, xor_2_out, xor_3_out, xor_4_out,
       xor_5_out, xor_6_out, xor_7_out, xor_8_out;

  xor xor_1 (xor_1_out, B[7], SUB);
  xor xor_2 (xor_2_out, B[6], SUB);
  xor xor_3 (xor_3_out, B[5], SUB);
  xor xor_4 (xor_4_out, B[4], SUB);
  xor xor_5 (xor_5_out, B[3], SUB);
  xor xor_6 (xor_6_out, B[2], SUB);
  xor xor_7 (xor_7_out, B[1], SUB);
  xor xor_8 (xor_8_out, B[0], SUB);
  _4bit_CLA u_4bit_cla_1 (
    .B3(xor_1_out), .A3(A[7]), .B2(xor_2_out), .A2(A[6]), .B1(xor_3_out), .A1(A[5]), .B0(xor_4_out),
    .A0(A[4]), .S3(SF), .C3(n4bit_cla_1_c3), .S2(Sum[6]), .S1(Sum[5]), .S0(Sum[4]), .Cout(n4bit_cla_1_cout),
    .Cin(n4bit_cla_2_cout));
  _4bit_CLA u_4bit_cla_2 (
    .B3(xor_5_out), .A3(A[3]), .B2(xor_6_out), .A2(A[2]), .B1(xor_7_out), .A1(A[1]), .B0(xor_8_out),
    .A0(A[0]), .S3(Sum[3]), .S2(Sum[2]), .S1(Sum[1]), .S0(Sum[0]), .Cout(n4bit_cla_2_cout), .Cin(Cin));  // open: C3
  xor xor_9 (CF, SUB, n4bit_cla_1_cout);
  xor xor_10 (OF, n4bit_cla_1_cout, n4bit_cla_1_c3);
  nor nor_1 (ZF, SF, Sum[6], Sum[5], Sum[4], Sum[3], Sum[2], Sum[1], Sum[0]);

  assign Sum[7] = SF;

  // Other names for the same wires on the sheet: A0_3[3:0] = A[3:0]; A4_7[3:0] = A[7:4]; B0_3[3:0] = B[3:0];
  //   B4_7[3:0] = B[7:4]; S0_3[3:0] = Sum[3:0]; S4_7[3:0] = {SF, Sum[6:4]}

  // Notes on the sheet:
  //   SUB: pull=down
  //   A: pull=down
  //   Cin: pull=down
  //   B: pull=down
endmodule

module _8bit_ALU (
  input  [7:0] A,
  input  [7:0] B,
  input  [3:0] Op,
  input  Cin,
  output CF,
  output ZF,
  output [7:0] Result
);

  wire multiplexer_1_out, multiplexer_2_out, not_1_out;
  wire [7:0] and_1_out, n8bit_cla_1_sum, or_1_out, xor_1_out;

  assign and_1_out = A & B;  // AND_Gate and_1, 8 bits wide
  assign or_1_out = A | B;  // OR_Gate or_1, 8 bits wide
  assign xor_1_out = A ^ B;  // XOR_Gate xor_1, 8 bits wide
  _8bit_CLA u_8bit_cla_1 (
    .B(B), .A(A), .SUB(Op[1]), .CF(CF), .ZF(ZF), .Sum(n8bit_cla_1_sum), .Cin(multiplexer_1_out));  // open: OF, SF
  Multiplexer #(.enable("false")) multiplexer_1 (
    .in0(Op[1]), .in1(multiplexer_2_out), .out(multiplexer_1_out), .sel(Op[0]));
  Multiplexer #(.enable("false")) multiplexer_2 (.in0(Cin), .in1(not_1_out), .out(multiplexer_2_out), .sel(Op[1]));
  not not_1 (not_1_out, Cin);
  Multiplexer #(.select(4), .width(8), .enable("false")) multiplexer_3 (
    .in0(n8bit_cla_1_sum), .in1(n8bit_cla_1_sum), .in2(n8bit_cla_1_sum), .in3(n8bit_cla_1_sum),
    .in4(and_1_out), .in5(or_1_out), .in6(xor_1_out), .in7(A), .in8(B), .out(Result), .sel(Op));  // open: in9, in10, in11, in12, in13, in14, in15

  // Notes on the sheet:
  //   A: pull=down
  //   Op: pull=down
  //   CF: pull=down
  //   ZF: pull=down
  //   Cin: pull=down
  //   B: pull=down
endmodule

module PC (
  input  [7:0] Data,
  input  Enable,
  input  Jump,
  input  Clock,
  input  Reset,
  output [7:0] PC
);

  wire [7:0] adder_1_out, multiplexer_1_out;

  Adder adder_1 (.a(8'h1), .b(PC), .out(adder_1_out));  // open: cin, cout
  Multiplexer #(.width(8)) multiplexer_1 (
    .in0(adder_1_out), .in1(Data), .out(multiplexer_1_out), .sel(Jump), .en(Enable));
  Register register_1 (.D(multiplexer_1_out), .Q(PC), .clk(Clock), .clr(Reset));  // open: en

  // Notes on the sheet:
  //   PC: pull=down
endmodule

module Decoder (
  input  [23:0] IR,
  output [3:0] rs2,
  output [3:0] rs1,
  output [3:0] rd,
  output RegWrite,
  output MemRead,
  output [7:0] Imm,
  output MemWrite,
  output BSrc,
  output BranchZ,
  output CWrite,
  output BranchNZ,
  output Jump,
  output OutEn,
  output [3:0] ALUop,
  output Halt
);

  wire ALUI1, ALUR0, LD4, LDA2, not_1_out, not_2_out, or_1_out, or_2_out, or_3_out, ST5, STA3;
  wire [3:0] multiplexer_1_out;

  Decoder_part #(.select(4), .enable("false")) decoder_1 (
    .out1(ALUR0), .out2(ALUI1), .out3(LDA2), .out4(STA3), .out5(LD4), .out6(ST5), .out7(BranchZ),
    .out8(BranchNZ), .out9(Jump), .out10(OutEn), .out11(Halt), .sel(IR[23:20]));  // open: out0, out12, out13, out14, out15
  or or_1 (or_1_out, ALUR0, ALUI1);
  not not_1 (not_1_out, IR[19]);
  not not_2 (not_2_out, IR[18]);
  or or_2 (or_2_out, LDA2, STA3);
  or or_3 (or_3_out, ALUR0, ALUI1);
  and and_1 (CWrite, or_1_out, not_1_out, not_2_out);
  Multiplexer #(.width(4), .enable("false")) multiplexer_1 (
    .in0(4'b0111), .in1(4'b1000), .out(multiplexer_1_out), .sel(or_2_out));
  Multiplexer #(.width(4), .enable("false")) multiplexer_2 (
    .in0(multiplexer_1_out), .in1(IR[19:16]), .out(ALUop), .sel(or_3_out));
  or or_4 (RegWrite, ALUR0, ALUI1, LDA2, LD4);
  or or_5 (MemRead, LDA2, LD4);
  or or_6 (MemWrite, STA3, ST5);
  or or_7 (BSrc, ALUI1, LDA2, STA3);

  assign Imm = IR[7:0];
  assign rd = IR[15:12];
  assign rs1 = IR[11:8];
  assign rs2 = IR[7:4];

  // Other names for the same wires on the sheet: BNZ7 = BranchNZ; BZ6 = BranchZ; HLT10 = Halt; IR_3_0[3:0] = IR[3:0];
  //   IR_7_4[3:0] = IR[7:4]; IR_11_8[3:0] = IR[11:8]; IR_15_12[3:0] = IR[15:12]; fn[3:0] = IR[19:16];
  //   IR_19_16[3:0] = IR[19:16]; IR_23_20[3:0] = IR[23:20]; op[3:0] = IR[23:20]; JMP8 = Jump; OUT9 = OutEn

  // Notes on the sheet:
  //   IR: pull=up
endmodule

module Registers (
  input  [7:0] Data,
  input  Write,
  input  [3:0] Address,
  input  [3:0] A_SEL,
  input  [3:0] B_SEL,
  input  Clock,
  input  Reset,
  output [7:0] A,
  output [7:0] B
);

  wire demultiplexer_1_out0, demultiplexer_1_out1, demultiplexer_1_out2, demultiplexer_1_out3,
       demultiplexer_1_out4, demultiplexer_1_out5, demultiplexer_1_out6, demultiplexer_1_out7,
       demultiplexer_1_out8, demultiplexer_1_out9, demultiplexer_1_out10, demultiplexer_1_out11,
       demultiplexer_1_out12, demultiplexer_1_out13, demultiplexer_1_out14, demultiplexer_1_out15;
  wire [7:0] register_1_q, register_2_q, register_3_q, register_4_q, register_5_q, register_6_q,
       register_7_q, register_8_q, register_9_q, register_10_q, register_11_q, register_12_q, register_13_q,
       register_14_q, register_15_q, register_16_q;

  Demultiplexer #(.select(4), .enable("false")) demultiplexer_1 (
    .out0(demultiplexer_1_out0), .out1(demultiplexer_1_out1), .out2(demultiplexer_1_out2),
    .out3(demultiplexer_1_out3), .out4(demultiplexer_1_out4), .out5(demultiplexer_1_out5),
    .out6(demultiplexer_1_out6), .out7(demultiplexer_1_out7), .out8(demultiplexer_1_out8),
    .out9(demultiplexer_1_out9), .out10(demultiplexer_1_out10), .out11(demultiplexer_1_out11),
    .out12(demultiplexer_1_out12), .out13(demultiplexer_1_out13), .out14(demultiplexer_1_out14),
    .out15(demultiplexer_1_out15), .in(Write), .sel(Address));
  Register #(.trigger("falling")) register_1 (
    .D(Data), .en(demultiplexer_1_out1), .Q(register_1_q), .clk(Clock), .clr(Reset));
  Register #(.trigger("falling")) register_2 (
    .D(Data), .en(demultiplexer_1_out0), .Q(register_2_q), .clk(Clock), .clr(Reset));
  Register #(.trigger("falling")) register_3 (
    .D(Data), .en(demultiplexer_1_out2), .Q(register_3_q), .clk(Clock), .clr(Reset));
  Register #(.trigger("falling")) register_4 (
    .D(Data), .en(demultiplexer_1_out3), .Q(register_4_q), .clk(Clock), .clr(Reset));
  Register #(.trigger("falling")) register_5 (
    .D(Data), .en(demultiplexer_1_out5), .Q(register_5_q), .clk(Clock), .clr(Reset));
  Register #(.trigger("falling")) register_6 (
    .D(Data), .en(demultiplexer_1_out4), .Q(register_6_q), .clk(Clock), .clr(Reset));
  Register #(.trigger("falling")) register_7 (
    .D(Data), .en(demultiplexer_1_out6), .Q(register_7_q), .clk(Clock), .clr(Reset));
  Register #(.trigger("falling")) register_8 (
    .D(Data), .en(demultiplexer_1_out7), .Q(register_8_q), .clk(Clock), .clr(Reset));
  Register #(.trigger("falling")) register_9 (
    .D(Data), .en(demultiplexer_1_out9), .Q(register_9_q), .clk(Clock), .clr(Reset));
  Register #(.trigger("falling")) register_10 (
    .D(Data), .en(demultiplexer_1_out8), .Q(register_10_q), .clk(Clock), .clr(Reset));
  Register #(.trigger("falling")) register_11 (
    .D(Data), .en(demultiplexer_1_out10), .Q(register_11_q), .clk(Clock), .clr(Reset));
  Register #(.trigger("falling")) register_12 (
    .D(Data), .en(demultiplexer_1_out11), .Q(register_12_q), .clk(Clock), .clr(Reset));
  Register #(.trigger("falling")) register_13 (
    .D(Data), .en(demultiplexer_1_out13), .Q(register_13_q), .clk(Clock), .clr(Reset));
  Register #(.trigger("falling")) register_14 (
    .D(Data), .en(demultiplexer_1_out12), .Q(register_14_q), .clk(Clock), .clr(Reset));
  Register #(.trigger("falling")) register_15 (
    .D(Data), .en(demultiplexer_1_out14), .Q(register_15_q), .clk(Clock), .clr(Reset));
  Register #(.trigger("falling")) register_16 (
    .D(Data), .en(demultiplexer_1_out15), .Q(register_16_q), .clk(Clock), .clr(Reset));
  Multiplexer #(.select(4), .width(8), .enable("false")) multiplexer_1 (
    .in0(register_2_q), .in1(register_1_q), .in2(register_3_q), .in3(register_4_q), .in4(register_6_q),
    .in5(register_5_q), .in6(register_7_q), .in7(register_8_q), .in8(register_10_q), .in9(register_9_q),
    .in10(register_11_q), .in11(register_12_q), .in12(register_14_q), .in13(register_13_q),
    .in14(register_15_q), .in15(register_16_q), .out(A), .sel(A_SEL));
  Multiplexer #(.select(4), .width(8), .enable("false")) multiplexer_2 (
    .in0(register_2_q), .in1(register_1_q), .in2(register_3_q), .in3(register_4_q), .in4(register_6_q),
    .in5(register_5_q), .in6(register_7_q), .in7(register_8_q), .in8(register_10_q), .in9(register_9_q),
    .in10(register_11_q), .in11(register_12_q), .in12(register_14_q), .in13(register_13_q),
    .in14(register_15_q), .in15(register_16_q), .out(B), .sel(B_SEL));
endmodule

module Stop (
  input  [3:0] ID_EX_rd,
  input  [3:0] rA,
  input  [3:0] rB,
  input  ID_EX_RegWrite,
  input  ID_EX_MemRead,
  output stall,
  output nstall
);

  wire and_1_out, comparator_1_eq, comparator_2_eq, or_1_out;

  Comparator #(.width(4)) comparator_1 (.a(ID_EX_rd), .b(rA), .eq(comparator_1_eq));  // open: gt, lt
  Comparator #(.width(4)) comparator_2 (.a(ID_EX_rd), .b(rB), .eq(comparator_2_eq));  // open: gt, lt
  or or_1 (or_1_out, comparator_1_eq, comparator_2_eq);
  and and_1 (and_1_out, or_1_out, ID_EX_RegWrite);
  and and_2 (stall, and_1_out, ID_EX_MemRead);
  not not_1 (nstall, stall);
endmodule

module forwarding_unit (
  input  [7:0] ID_EX_ReadData,
  input  [7:0] EX_MEM_ALUResult,
  input  [7:0] MEM_WB_ALUResult,
  input  [7:0] MEM_WB_MemData,
  input  MEM_WB_MemRead,
  input  [3:0] Src,
  input  [3:0] EX_MEM_rd,
  input  Ex_MEM_RegWrite,
  input  EX_MEM_MemRead,
  input  [3:0] MEM_WB_rd,
  input  MEM_WB_RegWrite,
  output [7:0] out_12
);

  wire comparator_1_eq, comparator_2_eq, hit1, hit2, not_1_out;
  wire [7:0] WBValue;

  Comparator #(.width(4)) comparator_1 (.a(Src), .b(EX_MEM_rd), .eq(comparator_1_eq));  // open: gt, lt
  not not_1 (not_1_out, EX_MEM_MemRead);
  Multiplexer #(.width(8), .enable("false")) multiplexer_1 (
    .in0(MEM_WB_ALUResult), .in1(MEM_WB_MemData), .out(WBValue), .sel(MEM_WB_MemRead));
  Comparator #(.width(4)) comparator_2 (.a(Src), .b(MEM_WB_rd), .eq(comparator_2_eq));  // open: gt, lt
  and and_1 (hit1, comparator_1_eq, Ex_MEM_RegWrite, not_1_out);
  and and_2 (hit2, comparator_2_eq, MEM_WB_RegWrite);
  Multiplexer #(.select(2), .width(8), .enable("false")) multiplexer_2 (
    .in0(ID_EX_ReadData), .in1(WBValue), .in2(EX_MEM_ALUResult), .in3(EX_MEM_ALUResult), .out(out_12),
    .sel({hit1, hit2}));
endmodule

module IR (
  input  Flush,
  input  [23:0] IR_input,
  input  Reset,
  input  Enable,
  input  Clock,
  output [23:0] IR_output
);

  wire [23:0] multiplexer_1_out;

  Multiplexer #(.width(24), .enable("false")) multiplexer_1 (
    .in0(IR_input), .in1({24{1'b0}}), .out(multiplexer_1_out), .sel(Flush));
  Register #(.width(24)) IR (.D(multiplexer_1_out), .en(Enable), .Q(IR_output), .clk(Clock), .clr(Reset));

  // Notes on the sheet:
  //   IR_input: pull=up
endmodule

module ID_EX (
  input  [7:0] Imm,
  input  flush,
  input  [7:0] ReadA,
  input  [7:0] ReadB,
  input  [3:0] ALUop,
  input  Enable,
  input  [3:0] rsA,
  input  Clock,
  input  [3:0] rsB,
  input  Reset,
  input  [3:0] rdC,
  input  RegWrite,
  input  MemWrite,
  input  MemRead,
  input  BSrc,
  input  BZ,
  input  BNZ,
  input  JMP,
  input  CWrite,
  input  OutEn,
  input  Halt,
  output [7:0] Imm_2,
  output [7:0] ReadA_2,
  output [7:0] ReadB_2,
  output [3:0] ALUop_2,
  output [3:0] rsA_2,
  output [3:0] rsB_2,
  output [3:0] rdC_2,
  output RegWrite_2,
  output MemWrite_2,
  output MemRead_2,
  output BSrc_2,
  output BZ_2,
  output BNZ_2,
  output JMP_2,
  output CWrite_2,
  output OutEn_2,
  output Halt_2
);

  wire [31:0] multiplexer_1_out, multiplexer_2_out;
  wire [31:24] ID_EX_q;
  wire [31:26] ID_EX2_q;

  Multiplexer #(.width(32), .enable("false")) multiplexer_1 (
    .in0({{8{1'b0}}, ReadB, ReadA, Imm}), .in1({32{1'b0}}), .out(multiplexer_1_out), .sel(flush));
  Multiplexer #(.width(32), .enable("false")) multiplexer_2 (
    .in0({{6{1'b0}}, Halt, OutEn, CWrite, JMP, BNZ, BZ, BSrc, MemRead, MemWrite, RegWrite, rdC, rsB, rsA, ALUop}),
    .in1({32{1'b0}}), .out(multiplexer_2_out), .sel(flush));
  Register #(.width(32)) ID_EX (
    .D(multiplexer_1_out), .en(Enable), .Q({ID_EX_q, ReadB_2, ReadA_2, Imm_2}), .clk(Clock), .clr(Reset));
  Register #(.width(32)) ID_EX2 (
    .D(multiplexer_2_out), .en(Enable),
    .Q({ID_EX2_q, Halt_2, OutEn_2, CWrite_2, JMP_2, BNZ_2, BZ_2, BSrc_2, MemRead_2, MemWrite_2, RegWrite_2, rdC_2, rsB_2, rsA_2, ALUop_2}),
    .clk(Clock), .clr(Reset));

  // Notes on the sheet:
  //   RegWrite: pull=down
  //   BSrc: pull=down
  //   ReadB: pull=down
  //   rsB: pull=down
  //   rsA: pull=down
  //   Halt: pull=down
  //   JMP: pull=down
  //   BZ: pull=down
  //   CWrite: pull=down
  //   rdC: pull=down
  //   MemRead: pull=down
  //   BNZ: pull=down
  //   Imm: pull=down
  //   OutEn: pull=down
  //   ALUop: pull=down
  //   MemWrite: pull=down
  //   ReadA: pull=down
endmodule

module EX_MEM (
  input  [7:0] ALUResult,
  input  [7:0] WriteData,
  input  [3:0] rd,
  input  RegWrite,
  input  MemWrite,
  input  MemRead,
  input  OutEn,
  input  Halt,
  input  Enable,
  input  Reset,
  input  Clock,
  output [7:0] ALUResult_2,
  output [7:0] WriteData_2,
  output [3:0] rd_2,
  output RegWrite_2,
  output MemWrite_2,
  output MemRead_2,
  output OutEn_2,
  output Halt_2
);

  wire [31:25] EX_MEM_q;

  Register #(.width(32)) EX_MEM (
    .D({{7{1'b0}}, Halt, OutEn, MemRead, MemWrite, RegWrite, rd, WriteData, ALUResult}), .en(Enable),
    .Q({EX_MEM_q, Halt_2, OutEn_2, MemRead_2, MemWrite_2, RegWrite_2, rd_2, WriteData_2, ALUResult_2}),
    .clk(Clock), .clr(Reset));

  // Notes on the sheet:
  //   WriteData: pull=down
  //   rd: pull=down
  //   RegWrite: pull=down
  //   MemWrite: pull=down
  //   Halt: pull=down
  //   MemRead: pull=down
  //   ALUResult: pull=down
  //   OutEn: pull=down
endmodule

module MEM_WB (
  input  [7:0] ALUResult,
  input  [7:0] MemData,
  input  [3:0] rd,
  input  RegWrite,
  input  MemRead,
  input  OutEn,
  input  Halt,
  input  Enable,
  input  Reset,
  input  Clock,
  output [7:0] ALUResult_2,
  output [7:0] MemData_2,
  output [3:0] rd_2,
  output RegWrite_2,
  output MemRead_2,
  output OutEn_2,
  output Halt_2
);

  wire [31:24] MEM_EX_q;

  Register #(.width(32)) MEM_EX (
    .D({{8{1'b0}}, Halt, OutEn, MemRead, RegWrite, rd, MemData, ALUResult}), .en(Enable),
    .Q({MEM_EX_q, Halt_2, OutEn_2, MemRead_2, RegWrite_2, rd_2, MemData_2, ALUResult_2}), .clk(Clock),
    .clr(Reset));

  // Notes on the sheet:
  //   ALUResult: pull=down
  //   MemRead: pull=down
  //   OutEn: pull=down
  //   rd: pull=down
  //   RegWrite: pull=down
  //   MemData: pull=down
  //   Halt: pull=down
endmodule

module CFRegister (
  input  CF,
  input  Enable,
  input  Reset,
  input  Clock,
  output C_Q
);

  Register #(.width(1)) register_1 (.D(CF), .en(Enable), .Q(C_Q), .clk(Clock), .clr(Reset));
endmodule

module OutPutRegister (
  input  [7:0] Input,
  input  Enable,
  input  Reset,
  input  Clock,
  output [7:0] Output
);

  Register register_1 (.D(Input), .en(Enable), .Q(Output), .clk(Clock), .clr(Reset));
endmodule
